# Fritzing sketch Programming (saved by Fritzing 0.9.3b)

parts:
  Debugger2 = Debugger
  ESP3 = ESP8266-07 [part_number=ESP8266]

nets:
  N1: Debugger2.3v, ESP3.CH_PD, ESP3.VCC
  GND: Debugger2.GND, ESP3.GND, ESP3.GPIO_15, ESP3.GPIO_0
  N2: Debugger2.RX, ESP3.TXD
  N3: Debugger2.TX, ESP3.RXD

custom parts:
  ESP8266-07: ESP8266 - 07 WiFi Module with adaptor plate
