# Fritzing sketch ProjectPrototype (saved by Fritzing 0.9.3b)
breadboards: 1

parts:
  WeMos_D1_Mini1 = WeMos D1 Mini
  M2 = BME280
  ZS-042_RTC2 = ZS-042 RTC Module

nets:
  3V3: WeMos_D1_Mini1.3V3, M2.VIN, ZS-042_RTC2.VCC
  N1: WeMos_D1_Mini1.D1, M2.SCL, ZS-042_RTC2.SCL
  N2: WeMos_D1_Mini1.D2, M2.SDA, ZS-042_RTC2.SDA
  GND: WeMos_D1_Mini1.G, M2.GND, ZS-042_RTC2.GND

custom parts:
  BME280: Temperature Humidity Barometric presure Sensor
