# Fritzing sketch ProjectSketch (saved by Fritzing 0.9.3b)
perfboards: 1

parts:
  ESP1 = ESP8266-07 [part_number=ESP8266]
  U1 = Battery Holders [package=lipo-1100mAh]
  TP1 = TP4056 [chip_label=TP4056 package="DIP (Dual Inline) [THT]"]
  M1 = BME280
  ZS-042_RTC1 = ZS-042 RTC Module
  IC2 = Voltage Regulator [package=78xxl]
  C1 = Ceramic Capacitor [capacitance=100nF package="100 mil [THT, multilayer]"]
  C2 = Ceramic Capacitor [capacitance=100nF package="200 mil [THT, multilayer]"]
  Part1 = Solar Cell

nets:
  VCC: ESP1.VCC, TP1.pin3, M1.VIN, ZS-042_RTC1.VCC
  GND: ESP1.GND, TP1.pin6, M1.GND, ZS-042_RTC1.GND
  N1: ESP1.GPIO_4, M1.SDA, ZS-042_RTC1.SDA
  N2: ESP1.GPIO_5, M1.SCL, ZS-042_RTC1.SCL
  N3: U1.+, TP1.pin4
  N4: U1.-, TP1.pin5
  N5: TP1.pin1, IC2.OUT, C1.0
  N6: TP1.pin2, IC2.GND, C1.1, C2.0, Part1.-
  N7: IC2.IN, C2.1, Part1.+

custom parts:
  ESP8266-07: ESP8266 - 07 WiFi Module with adaptor plate
  TP4056: A DIP stand-in part for whatever IC you want. With 6 pins on a 300mil dual inline package (DIP) footprint.
  BME280: Temperature Humidity Barometric presure Sensor
